// Logisim project codificador.circ as structural Verilog: 1 circuit, main circuit main
module main (
  input  e0,
  input  e1,
  input  e2,
  input  e3,
  output s0,
  output s1,
  output v
);

  wire and_1_out, and_2_out, and_3_out, not_1_out, not_2_out, not_3_out, not_4_out;

  ExactlyOne xor_1 (.out(v), .in0(e0), .in1(e1), .in3(e2), .in4(e3));
  not not_1 (not_1_out, e0);
  not not_2 (not_2_out, e1);
  not not_3 (not_3_out, e2);
  not not_4 (not_4_out, e3);
  and and_1 (and_1_out, not_1_out, not_3_out, not_4_out, e1);
  and and_2 (and_2_out, not_2_out, not_1_out, not_4_out, e2);
  and and_3 (and_3_out, not_3_out, not_1_out, not_2_out, e3);
  or or_1 (s0, and_1_out, and_3_out);
  or or_2 (s1, and_2_out, and_3_out);
endmodule
